// Logisim project Exercícios ARQ.circ as structural Verilog
module FF_D (
  input  D,
  input  CLK,
  output Q,
  output Q_prime
);

  wire and_1_out, and_2_out, not_1_out;

  not not_1 (not_1_out, D);
  and and_1 (and_1_out, D, CLK);
  and and_2 (and_2_out, not_1_out, CLK);
  nor nor_1 (Q, and_1_out, Q_prime);
  nor nor_2 (Q_prime, Q, and_2_out);
endmodule

module FF_T (
  input  T,
  input  CLK,
  output Q,
  output Q_prime
);

  wire and_1_out, and_2_out;

  and and_1 (and_1_out, T, CLK);
  and and_2 (and_2_out, CLK, T);
  nor nor_1 (Q, and_1_out, Q_prime);
  nor nor_2 (Q_prime, and_2_out, Q);
endmodule

module FF_JK (
  input  in_1,
  input  in_2,
  input  in_3,
  output out_4,
  output out_5
);

  wire and_1_out, and_2_out;

  and and_1 (and_1_out, in_1, out_4, in_2);
  and and_2 (and_2_out, in_3, out_5, in_2);
  nor nor_1 (out_4, and_1_out, out_5);
  nor nor_2 (out_5, out_4, and_2_out);
endmodule

module FF_T_com_load__sPRE_e_sCLR (
  input  sPRE,
  input  T,
  input  PRE,
  input  CLK,
  input  EN,
  input  sCLR,
  input  CLR,
  output Q,
  output Q_prime
);

  wire and_1_out, and_2_out, not_1_out, not_2_out, or_1_out, or_2_out;

  or or_1 (or_1_out, sPRE, T);
  not not_1 (not_1_out, sPRE);
  not not_2 (not_2_out, sCLR);
  and and_1 (and_1_out, not_1_out, T);
  and and_2 (and_2_out, or_1_out, not_2_out);
  or or_2 (or_2_out, and_1_out, sCLR);
  J_K_Flip_Flop j_k_ff_1 (
    .J(and_2_out), .clk(CLK), .K(or_2_out), .Q(Q), .Qn(Q_prime), .preset(PRE), .en(EN), .reset(CLR));
endmodule

module Q1___reg4BitsLoad (
  input  EO,
  input  CLK,
  input  LOAD,
  input  D3,
  input  D2,
  input  D1,
  input  D0,
  output Q3,
  output Q2,
  output Q1,
  output Q0
);

  wire d_ff_1_q, d_ff_2_q, d_ff_3_q, d_ff_4_q;

  assign Q3 = EO ? d_ff_1_q : 1'bz;  // Controlled_Buffer controlled_buffer_1
  D_Flip_Flop d_ff_1 (.clk(CLK), .D(D3), .Q(d_ff_1_q), .preset(1'b0), .en(LOAD), .reset(1'b0));  // open: Qn
  assign Q2 = EO ? d_ff_2_q : 1'bz;  // Controlled_Buffer controlled_buffer_2
  D_Flip_Flop d_ff_2 (.clk(CLK), .D(D2), .Q(d_ff_2_q), .preset(1'b0), .en(LOAD), .reset(1'b0));  // open: Qn
  D_Flip_Flop d_ff_3 (.clk(CLK), .D(D1), .Q(d_ff_3_q), .preset(1'b0), .en(LOAD), .reset(1'b0));  // open: Qn
  assign Q1 = EO ? d_ff_3_q : 1'bz;  // Controlled_Buffer controlled_buffer_3
  assign Q0 = EO ? d_ff_4_q : 1'bz;  // Controlled_Buffer controlled_buffer_4
  D_Flip_Flop d_ff_4 (.clk(CLK), .D(D0), .Q(d_ff_4_q), .preset(1'b0), .en(LOAD), .reset(1'b0));  // open: Qn

  // Notes on the sheet:
  //   Implemente um Registrador de dados com entrada e saídas paralelas, sinal de load e de EO
endmodule

module Q3___Contador_em_Anel (
  input  Clk,
  input  Inicio,
  output Q0,
  output Q1,
  output Q2,
  output out_6,
  output Q3
);

  D_Flip_Flop d_ff_1 (.clk(Clk), .D(out_6), .Q(Q0), .preset(Inicio));  // open: Qn, en, reset
  D_Flip_Flop d_ff_2 (.clk(Clk), .D(Q0), .Q(Q1), .reset(Inicio));  // open: Qn, preset, en
  D_Flip_Flop d_ff_3 (.clk(Clk), .D(Q1), .Q(Q2), .reset(Inicio));  // open: Qn, preset, en
  D_Flip_Flop d_ff_4 (.clk(Clk), .D(Q2), .Q(out_6), .reset(Inicio));  // open: Qn, preset, en

  assign Q3 = out_6;

  // Notes on the sheet:
  //   Determine o diagrama de transição de estados do contador em anel abaixo:
  //   DIAGRAMA: Inicio  ->  1  ->  2  ->  4  ->  8  ->  1  ->  2  ->  4  ->  8  ->  1  ->  ...
endmodule

module Q4___Tabelas_Verdade_dos_FF (
);


  // Notes on the sheet:
  //   J
  //   K
  //   ---------------------
  //   0
  //   1
  //   0
  //   0
  //   1
  //   1
  //   1
  //   D
  //   ---------------------
  //   0
  //   1
  //   FF JK
  //   Q'
  //   Q
  //   ------|---------------
  //   |
  //   Q'
  //   Q
  //   0
  //   |
  //   |
  //   |
  //   |
  //   |
  //   |
  //   |
  //   |
  //   0
  //   1
  //   |
  //   |
  //   |
  //   |
  //   |
  //   0
  //   1
  //   |
  //   |
  //   |
  //   |
  //   |
  //   |
  //   |
  //   TROCA
  //   |
  //   |
  //   |
  //   FF D
  //   Q'
  //   Q
  //   ------|---------------
  //   |
  //   |
  //   0
  //   |
  //   1
  //   |
  //   |
  //   |
  //   |
  //   |
  //   |
  //   1
  //   0
  //   |
  //   |
  //   |
  //   |
  //   |
  //   |
  //   |
  //   |
  //   |
  //   |
  //   |
  //   |
  //   |
  //   |
  //   |
  //   S
  //   0
  //   0
  //   1
  //   1
  //   Dê a tabela verdade dos flip-flops: JK, SR, D, T
  //   FF SR
  //   Q
  //   R
  //   ---------------------
  //   |
  //   0
  //   Q
  //   |
  //   |
  //   |
  //   |
  //   |
  //   |
  //   0
  //   |
  //   1
  //   |
  //   |
  //   |
  //   |
  //   |
  //   1
  //   0
  //   |
  //   |
  //   |
  //   |
  //   |
  //   0
  //   |
  //   |
  //   |
  //   |
  //   |
  //   |
  //   FF T
  //   T
  //   ---------------------
  //   |
  //   |
  //   0
  //   |
  //   |
  //   |
  //   |
  //   |
  //   |
  //   |
  //   |
  //   |
  //   |
  //   1
  //   |
  //   |
  //   |
  //   |
  //   |
  //   |
  //   |
  //   |
  //   |
  //   |
  //   |
  //   |
  //   Q'
  //   ------|---------------
  //   Q'
  //   1
  //   0
  //   PROIBIDO
  //   Q'
  //   Q
  //   ------|---------------
  //   Q
  //   Q'
  //   TROCA
endmodule

module Q5___FF_D_com_FF_T (
  input  D
);

  wire ff_t_1_q, xor_1_out;

  xor xor_1 (xor_1_out, D, ff_t_1_q);
  FF_T ff_t_1 (.T(xor_1_out), .Q(ff_t_1_q));  // open: CLK, Q_prime

  // Notes on the sheet:
  //   Implemente um flip-flop tipo D usando flip-flop tipo T e portas lógicas
endmodule

module Q6___FF_T_com_FF_D (
  input  T
);

  wire ff_d_1_q, xor_1_out;

  xor xor_1 (xor_1_out, ff_d_1_q, T);
  FF_D ff_d_1 (.D(xor_1_out), .Q(ff_d_1_q));  // open: Q_prime, CLK

  // Notes on the sheet:
  //   Implemente um flip-flop tipo T usando flip-flop tipo D e portas lógicas
endmodule

module Q7___Contador_up_down (
  input  CLK,
  input  CLR_ass,
  input  U_D,
  output Q0,
  output Q1,
  output Q2,
  output Q3
);

  wire and_1_out, and_2_out, and_3_out, xor_1_out, xor_2_out, xor_3_out, xor_4_out;

  and and_1 (and_1_out, U_D, Q0);
  D_Flip_Flop d_ff_1 (.clk(CLK), .D(xor_1_out), .Q(Q0), .reset(CLR_ass));  // open: Qn, preset, en
  xor xor_1 (xor_1_out, Q0, U_D);
  D_Flip_Flop d_ff_2 (.clk(CLK), .D(xor_2_out), .Q(Q1), .reset(CLR_ass));  // open: Qn, preset, en
  ExactlyOne xor_2 (.out(xor_2_out), .in0(and_1_out), .in1(Q1), .in4(U_D));
  and and_2 (and_2_out, U_D, Q0, Q1);
  D_Flip_Flop d_ff_3 (.clk(CLK), .D(xor_3_out), .Q(Q2), .reset(CLR_ass));  // open: Qn, preset, en
  ExactlyOne xor_3 (.out(xor_3_out), .in0(and_2_out), .in3(Q2), .in4(U_D));
  and and_3 (and_3_out, U_D, Q0, Q1, Q2);
  D_Flip_Flop d_ff_4 (.clk(CLK), .D(xor_4_out), .Q(Q3), .reset(CLR_ass));  // open: Qn, preset, en
  ExactlyOne xor_4 (.out(xor_4_out), .in0(Q3), .in1(and_3_out), .in4(U_D));

  // Notes on the sheet:
  //   Implemente um contador um/down módulo 16, síncrono, com entrada de clear assíncrono
endmodule

module Q8___FSM_3_9_6_12 (
  input  CLK,
  output S0,
  output S1,
  output S2,
  output S3
);

  D_Flip_Flop d_ff_1 (.clk(CLK), .Q(S0));  // open: D, Qn, preset, en, reset
  D_Flip_Flop d_ff_2 (.clk(CLK), .Q(S1));  // open: D, Qn, preset, en, reset
  D_Flip_Flop d_ff_3 (.clk(CLK), .Q(S2));  // open: D, Qn, preset, en, reset
  D_Flip_Flop d_ff_4 (.clk(CLK), .Q(S3));  // open: D, Qn, preset, en, reset

  // Notes on the sheet:
  //   Implemente uma máquina de estados finita que realize o seguinte diagrama de estados: INICIO -> 3 -> 9 -> 6 -> 12 -> 3 -> 9 -> ...
endmodule

module Q10___Diagrama_do_circuito (
  input  in_1,
  input  in_2,
  output out_3,
  output out_4
);

  wire j_k_ff_1_qn, j_k_ff_2_qn;

  J_K_Flip_Flop j_k_ff_1 (
    .J(j_k_ff_2_qn), .clk(in_1), .K(out_4), .Q(out_3), .Qn(j_k_ff_1_qn), .reset(in_2));  // open: preset, en
  J_K_Flip_Flop j_k_ff_2 (
    .J(out_3), .clk(in_1), .K(j_k_ff_1_qn), .Q(out_4), .Qn(j_k_ff_2_qn), .reset(in_2));  // open: preset, en

  // Notes on the sheet:
  //   Determine o diagrama de estados do circuito abaixo:
  //   Diagrama: Inicio -> 0  ->  3  ->  2  ->  1  ->  0  ->  3  ->  2  ->  1  ->  0  ->  3  -> ...
endmodule

module contador_mod_16 (
  input  in_1,
  input  in_2,
  output out_3,
  output out_4,
  output out_5,
  output out_6
);

  T_Flip_Flop t_ff_1 (.clk(in_2), .T(in_1), .Qn(out_3));  // open: Q, preset, reset, en
  T_Flip_Flop t_ff_2 (.clk(out_3), .T(in_1), .Qn(out_4));  // open: Q, preset, reset, en
  T_Flip_Flop t_ff_3 (.clk(out_4), .T(in_1), .Qn(out_5));  // open: Q, preset, reset, en
  T_Flip_Flop t_ff_4 (.clk(out_5), .T(in_1), .Qn(out_6));  // open: Q, preset, reset, en
endmodule
