// Logisim project contadorMod16.circ as structural Verilog: 1 circuit, main circuit main
module main (
  input  Q0,
  input  Q1,
  input  Q2,
  input  Q3,
  output CLK,
  output CLR,
  output U_D
);

  wire d_ff_1_p2, d_ff_2_p2, d_ff_3_p2, d_ff_4_qn, undriven, undriven_2, undriven_3;

  // D_Flip_Flop #(.clock("CLK"), .clear("CLR")) d_ff_1: pin names not known; wires that end beside it: Q0, d_ff_1_p2
  buf xor_1 (Q0, undriven);  // XOR_Gate
  // D_Flip_Flop #(.clock("CLK"), .clear("CLR")) d_ff_2: pin names not known; wires that end beside it: Q0, d_ff_2_p2
  xor xor_2 (Q0, undriven, undriven_2);
  // D_Flip_Flop #(.clock("CLK"), .clear("CLR")) d_ff_3: pin names not known; wires that end beside it: Q0, d_ff_3_p2
  xor xor_3 (Q0, undriven_2, undriven_3);
  D_Flip_Flop #(.clock("CLK"), .clear("CLR")) d_ff_4 (.Q(Q0), .Qn(d_ff_4_qn));  // open: clk, D, preset, en, reset
  buf xor_4 (Q0, undriven_3);  // XOR_Gate
  and and_1 (Q0, d_ff_1_p2, Q0, d_ff_2_p2);
  and and_2 (Q0, d_ff_2_p2, Q0, d_ff_3_p2);
  and and_3 (Q0, d_ff_3_p2, Q0, d_ff_4_qn);

  assign CLK = Q0;
  assign CLR = Q0;
  assign Q1 = Q0;
  assign Q2 = Q0;
  assign Q3 = Q0;
  assign U_D = Q0;
endmodule
